# Fritzing sketch Cablage detection anomalie (saved by Fritzing 0.9.3b)
breadboards: 1

parts:
  Composant1 = Arduino Uno (Rev3)
  J1 = Piezo Speaker
  LED1 = LED - 5mm [color="Red (633nm)" package="5 mm [THT]"]
  Grove1 = Grove OLED 128x96
  R1 = Rotary Potentiometer (Small) [maximum_resistance=100kΩ package=THT]
  R2 = Rotary Potentiometer (Small) [maximum_resistance=100kΩ package=THT]
  R3 = Rotary Potentiometer (Small) [maximum_resistance=100kΩ package=THT]

nets:
  N1: Composant1.A0, R3.wiper
  N2: Composant1.A1, R2.wiper
  N3: Composant1.A2, R1.wiper
  N4: Composant1.A4/SDA, Grove1.SDA
  N5: Composant1.A5/SCL, Grove1.SCL
  N6: Composant1.D9_PWM, J1.pin2
  N7: Composant1.D10_PWM/SS, LED1.anode
  5V: Composant1.5V, Grove1.VCC, R1.leg1, R2.leg1, R3.leg1
  GND: Composant1.GND, J1.pin1, LED1.cathode, Grove1.GND, R1.leg2, R2.leg2, R3.leg2
