# Fritzing sketch Cablage alarme (saved by Fritzing 0.9.3b)
breadboards: 1

parts:
  Composant1 = Arduino Uno (Rev3)
  J1 = Piezo Speaker
  LED1 = LED - 5mm [color="Red (633nm)" package="5 mm [THT]"]

nets:
  N1: Composant1.D9_PWM, J1.pin2
  N2: Composant1.D10_PWM/SS, LED1.anode
  N3: Composant1.GND, J1.pin1, LED1.cathode
